# Fritzing sketch Esquema (saved by Fritzing 0.9.2b)
breadboards: 1

parts:
  Raspberry_Pi_1 = Raspberry Pi 3 [part_number=RPI-3-V1.2]
  LED1 = LED - 5mm [color="Green (570nm)" package="5 mm [THT]"]
  LED2 = LED - 5mm [color="Yellow (592nm)" package="5 mm [THT]"]
  LED3 = LED - 5mm [color="Red (633nm)" package="5 mm [THT]"]

nets:
  N1: Raspberry_Pi_1.GIPO4, LED3.anode
  N2: Raspberry_Pi_1.GIPO17, LED1.anode
  N3: Raspberry_Pi_1.GIPO27, LED2.anode
  N4: Raspberry_Pi_1.GND, LED1.cathode, LED2.cathode, LED3.cathode
