# Fritzing sketch Esquema (saved by Fritzing 0.9.2b)
breadboards: 1

parts:
  Raspberry_Pi1 = Raspberry Pi 2
  R1 = Resistor [tolerance=±5% resistance=1k package=THT]
  S1 = Pushbutton [package="[THT]"]
  LED1 = LED - 5mm [color="Red (633nm)" package="5 mm [THT]"]
  LED2 = LED - 5mm [color="Yellow (592nm)" package="5 mm [THT]"]
  LED3 = LED - 5mm [color="Green (555nm)" package="5 mm [THT]"]
  LED4 = LED - 5mm [color="Red (633nm)" package="5 mm [THT]"]
  LED5 = LED - 5mm [color="Green (555nm)" package="5 mm [THT]"]

nets:
  N1: Raspberry_Pi1.GPIO4, LED3.anode
  N2: Raspberry_Pi1.GPIO17, LED2.anode
  N3: Raspberry_Pi1.GPIO27, LED1.anode
  N4: Raspberry_Pi1.GPIO22, R1.Pin_1, S1.Pin_3, S1.Pin_4
  N5: Raspberry_Pi1.GND, R1.Pin_0
  N6: Raspberry_Pi1.GPIO15, LED4.anode
  N7: Raspberry_Pi1.GPIO14, LED5.anode
  N8: Raspberry_Pi1.5V, S1.Pin_1, S1.Pin_2
  N9: LED1.cathode, LED2.cathode, LED3.cathode, LED4.cathode, LED5.cathode

notes:
  Alimentación 5V
  Tierra
