# Fritzing sketch Esquema (saved by Fritzing 0.9.2b)
breadboards: 1

parts:
  LED1 = RGB LED (com. cathode, rgb) [package="5 mm [THT]"]
  Raspberry_Pi1 = Raspberry Pi 2
  R2 = Resistor [tolerance=±5% resistance=100 package=THT]
  R3 = Resistor [tolerance=±5% resistance=100 package=THT]
  R1 = Resistor [tolerance=±5% resistance=100 package=THT]

nets:
  N1: LED1.red_anode, R1.Pin_0
  N2: LED1.common_cathode, Raspberry_Pi1.GND
  N3: LED1.green_anode, R2.Pin_0
  N4: LED1.blue_anode, R3.Pin_0
  N5: Raspberry_Pi1.GPIO18, R3.Pin_1
  N6: Raspberry_Pi1.GPIO15, R2.Pin_1
  N7: Raspberry_Pi1.GPIO14, R1.Pin_1
